// Logisim project SilogismosCategoricos.circ as structural Verilog: 11 circuits, main circuit main
module main (
  input  A,
  input  P_M,
  input  E,
  input  I,
  input  O,
  input  A_2,
  input  E_2,
  input  I_2,
  input  S_M,
  input  O_2,
  input  A_3,
  input  E_3,
  input  I_3,
  input  O_3,
  output Regra2,
  output M_P,
  output out_17,
  output out_18,
  output out_19,
  output M_S,
  output out_21,
  output out_22
);

  wire figuradistrib_1_distrpredicado, figuradistrib_1_distrsujeito, or_1_out, or_2_out, or_3_out, or_4_out,
       or_5_out, or_6_out, setfigura_1_a, setfigura_1_b, setfigura_1_c, setfigura_1_d, setfigura_1_e,
       setfigura_1_f, setfigura_1_g, termodistrb_1_out_6, termodistrb_2_out_6, termodistrb_3_out_6,
       termodistrb_4_out_6;

  _7_Segment_Display u_7_segment_display_1 (
    .g(setfigura_1_g), .f(setfigura_1_f), .a(setfigura_1_a), .b(setfigura_1_b), .e(setfigura_1_e),
    .d(setfigura_1_d), .c(setfigura_1_c));  // open: dp
  not not_1 (M_P, P_M);
  not not_2 (M_S, S_M);
  SetFigura setfigura_1 (
    .PremMaior(P_M), .PremMenor(S_M), .a(setfigura_1_a), .b(setfigura_1_b), .c(setfigura_1_c),
    .d(setfigura_1_d), .e(setfigura_1_e), .f(setfigura_1_f), .g(setfigura_1_g));
  TermoDistrb termodistrb_1 (.X_M(P_M), .A(A), .E(E), .I(I), .O(O), .out_6(termodistrb_1_out_6));
  TermoDistrb termodistrb_2 (.X_M(S_M), .A(A_2), .E(E_2), .I(I_2), .O(O_2), .out_6(termodistrb_2_out_6));
  FiguraDistrib figuradistrib_1 (
    .A(A_3), .E(E_3), .I(I_3), .O(O_3), .DistrSujeito(figuradistrib_1_distrsujeito),
    .DistrPredicado(figuradistrib_1_distrpredicado));
  TermoDistrb termodistrb_3 (.X_M(M_P), .A(A), .E(E), .I(I), .O(O), .out_6(termodistrb_3_out_6));
  TermoDistrb termodistrb_4 (.X_M(M_S), .A(A_2), .E(E_2), .I(I_2), .O(O_2), .out_6(termodistrb_4_out_6));
  or or_1 (or_1_out, E, O);
  or or_2 (or_2_out, E_2, O_2);
  or or_3 (or_3_out, A_3, I_3);
  or or_4 (or_4_out, A, E);
  or or_5 (or_5_out, E_2, A_2);
  or or_6 (or_6_out, I_3, O_3);
  Regra2 regra2_1 (.tmMaiorDistrb(termodistrb_1_out_6), .tmMenorDistrb(termodistrb_2_out_6), .ViolaRegra2(Regra2));
  Regra3 Regra3 (
    .PredDistrPM(termodistrb_3_out_6), .SujDistrPm(termodistrb_4_out_6),
    .PredDistrConc(figuradistrib_1_distrpredicado), .SujDistrConc(figuradistrib_1_distrsujeito),
    .FalaciaProcIlicitoTermoMaior(out_17), .FalaciaProcIlicitoTermoMenor(out_18));
  Regra4 Regra4 (.PMaior(or_1_out), .PMenor(or_2_out), .FalaciaDasPremissasExclusivas(out_19));
  Regra5 Regra5 (
    .PremMaior(or_1_out), .PremMenor(or_2_out), .Conclusao(or_3_out),
    .FalaciaDaConclusaoAfirmtvaAPartirPremNegativ(out_21));
  Regra6 Regra6 (
    .PremMaiorUniv(or_4_out), .PremMenorUniv(or_5_out), .ConclusaoParticular(or_6_out),
    .FalaciaExistencial(out_22));

  // Notes on the sheet:
  //   Premissa menor
  //   S-P
  //   Premissa maior
  //   Conclusão
  //   Silogismos categóricos de forma típica
  //   Fonte doutrinária: Introdução à Lógica - Irving Copi (Cap. 6)
  //   Falácia do termo médio não distribuído
  //   Falácia Ilícito Maior
  //   Falácia Ilícito Menor
  //   Falácia das premissas exclusivas
  //   Falc concl. positv sobre prem. ngtv
  //   Falacia existencial
endmodule

module Regra2 (
  input  tmMaiorDistrb,
  input  tmMenorDistrb,
  output ViolaRegra2
);

  wire not_1_out, not_2_out;

  not not_1 (not_1_out, tmMaiorDistrb);
  not not_2 (not_2_out, tmMenorDistrb);
  and and_1 (ViolaRegra2, not_1_out, not_2_out);
endmodule

module SetFigura (
  input  PremMaior,
  input  PremMenor,
  output a,
  output b,
  output c,
  output d,
  output e,
  output f,
  output g
);

  wire and_2_out, and_3_out, and_4_out, and_5_out, not_1_out, not_2_out, not_3_out, not_4_out, not_5_out,
       not_6_out, not_7_out, not_8_out;

  not not_1 (not_1_out, PremMaior);
  not not_2 (not_2_out, PremMenor);
  not not_3 (not_3_out, PremMaior);
  not not_4 (not_4_out, PremMenor);
  not not_5 (not_5_out, PremMaior);
  not not_6 (not_6_out, PremMenor);
  and and_1 (e, PremMaior, PremMenor);
  not not_7 (not_7_out, PremMenor);
  not not_8 (not_8_out, PremMenor);
  and and_2 (and_2_out, not_1_out, not_2_out);
  and and_3 (and_3_out, PremMaior, PremMenor);
  or or_1 (c, not_3_out, not_4_out);
  and and_4 (and_4_out, not_5_out, not_6_out);
  and and_5 (and_5_out, PremMaior, PremMenor);
  and and_6 (f, PremMaior, not_7_out);
  or or_2 (g, not_8_out, PremMaior);
  or or_3 (a, and_2_out, and_3_out);
  or or_4 (d, and_4_out, and_5_out);

  assign b = 1'b1;
endmodule

module DistribuiSP (
  input  bit1,
  input  bit0,
  output DistrSujeito,
  output DistrPredicado
);

  not not_1 (DistrSujeito, bit1);

  assign DistrPredicado = bit0;
endmodule

module ConverteRepresentacao (
  input  A,
  input  E,
  input  I,
  input  O,
  output bit1,
  output bit0
);

  wire not_1_out, not_2_out, not_3_out, not_4_out;

  not not_1 (not_1_out, A);
  and and_1 (bit1, not_1_out, not_2_out);
  not not_2 (not_2_out, E);
  not not_3 (not_3_out, A);
  and and_2 (bit0, not_3_out, not_4_out);
  not not_4 (not_4_out, I);
endmodule

module Regra3 (
  input  PredDistrPM,
  input  SujDistrPm,
  input  PredDistrConc,
  input  SujDistrConc,
  output FalaciaProcIlicitoTermoMaior,
  output FalaciaProcIlicitoTermoMenor
);

  wire and_2_out, and_3_out, not_1_out, not_2_out, not_3_out, not_4_out, not_5_out;

  not not_1 (not_1_out, PredDistrPM);
  not not_2 (not_2_out, PredDistrPM);
  not not_3 (not_3_out, SujDistrPm);
  not not_4 (not_4_out, SujDistrPm);
  not not_5 (not_5_out, PredDistrConc);
  and and_1 (FalaciaProcIlicitoTermoMaior, not_1_out, PredDistrConc);
  and and_2 (and_2_out, not_2_out, not_3_out, SujDistrConc);
  and and_3 (and_3_out, not_4_out, not_5_out, SujDistrConc);
  or or_1 (FalaciaProcIlicitoTermoMenor, and_2_out, and_3_out);
endmodule

module TermoDistrb (
  input  X_M,
  input  A,
  input  E,
  input  I,
  input  O,
  output out_6
);

  wire and_1_out, and_2_out, figuradistrib_1_distrpredicado, figuradistrib_1_distrsujeito, not_1_out;

  not not_1 (not_1_out, X_M);
  and and_1 (and_1_out, not_1_out, figuradistrib_1_distrsujeito);
  FiguraDistrib figuradistrib_1 (
    .A(A), .E(E), .I(I), .O(O), .DistrSujeito(figuradistrib_1_distrsujeito),
    .DistrPredicado(figuradistrib_1_distrpredicado));
  and and_2 (and_2_out, figuradistrib_1_distrpredicado, X_M);
  or or_1 (out_6, and_1_out, and_2_out);

  // Notes on the sheet:
  //   Premissa
  //   M-X
endmodule

module FiguraDistrib (
  input  A,
  input  E,
  input  I,
  input  O,
  output DistrSujeito,
  output DistrPredicado
);

  wire converterepresentacao_1_bit0, converterepresentacao_1_bit1;

  DistribuiSP distribuisp_1 (
    .bit1(converterepresentacao_1_bit1), .bit0(converterepresentacao_1_bit0), .DistrSujeito(DistrSujeito),
    .DistrPredicado(DistrPredicado));
  ConverteRepresentacao converterepresentacao_1 (
    .A(A), .E(E), .I(I), .O(O), .bit1(converterepresentacao_1_bit1), .bit0(converterepresentacao_1_bit0));
endmodule

module Regra4 (
  input  PMaior,
  input  PMenor,
  output FalaciaDasPremissasExclusivas
);

  and and_1 (FalaciaDasPremissasExclusivas, PMaior, PMenor);
endmodule

module Regra5 (
  input  PremMaior,
  input  PremMenor,
  input  Conclusao,
  output FalaciaDaConclusaoAfirmtvaAPartirPremNegativ
);

  wire or_1_out;

  or or_1 (or_1_out, PremMenor, PremMaior);
  and and_1 (FalaciaDaConclusaoAfirmtvaAPartirPremNegativ, or_1_out, Conclusao);
endmodule

module Regra6 (
  input  PremMaiorUniv,
  input  PremMenorUniv,
  input  ConclusaoParticular,
  output FalaciaExistencial
);

  and and_1 (FalaciaExistencial, PremMaiorUniv, PremMenorUniv, ConclusaoParticular);
endmodule
